# Fritzing sketch Untitled Sketch (saved by Fritzing 0.9.3b)
breadboards: 1

parts:
  WeMos_D1_Mini1 = WeMos D1 Mini
  M1 = 1 chan 5v relay module
  Grove1 = Grove Button
  LED1 = LED - 3mm [color="Red (633nm)" package="3 mm [THT]"]

nets:
  N1: WeMos_D1_Mini1.3V3, LED1.anode
  N2: M1.pin_1, M1.pin_4, M1.pin_5, Grove1.GND, LED1.cathode
  N3: M1.pin_2, Grove1.VCC

custom parts:
  1 chan 5v relay module: 1 Channel 5V Relay Module Board Shield with Optocoupler Support High and Low Level Trigger for Arduino.
